# Fritzing sketch ESP32-WebServerDHT11-OLED (saved by Fritzing 0.9.10b)
breadboards: 1

parts:
  M1 = DOIT Esp32 DevKit v1 (30 pins long, 11 pins width) [part_number=ESP32S-PIN30]
  RHT1 = Humidity and Temperature Sensor RHT03
  R1 = Resistor [tolerance=±5% power=0.25 resistance=10k package=THT]
  OLED1 = OLED 128x64 I2C Monochrome Display VDD-GND

nets:
  3V3: M1.3V3, RHT1.Vcc, R1.Pin_1, OLED1.VDD
  GND: M1.GND, RHT1.GND_2, OLED1.GND
  N1: M1.D4, RHT1.Data-signal, R1.Pin_0
  N2: M1.D21, OLED1.SDA
  N3: M1.D22, OLED1.SCK

custom parts:
  DOIT Esp32 DevKit v1 (30 pins long, 11 pins width): The DOIT Esp32 DevKit v1 is one of the development board created by DOIT to evaluate the ESP-WROOM-32 module. It is based on the ESP32 microcontroller that boasts Wifi, Bluetooth, Ethernet and Low Power support all in a single chip. (vanepp) made breadboard work, adjusted pin numbering and labels and reduced size of schematic and cleaned up pcb. This chip is 30pins long (2 x15) and 11 pins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
  OLED 128x64 I2C Monochrome Display VDD-GND: OLED 128x64 I2C Monochrome Display. Note: there are two variants of this part, this one is the VDD GND SCK SDA variant. The other is GND VDD SCK SDA. Make sure you select the part that matches your module as using the incorrect part will probably destroy your module! In addition the mounting holes are marked on silkscreen but not by default drilled. If you want drilled mounting holes, copy a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
